// Logisim project FidanIsmayilova_ALUDecoder.circ as structural Verilog: 1 circuit, main circuit main
module main (
  input  [3:0] Rd,
  input  RegW,
  input  Branch,
  output out_4
);

  wire and_1_out, and_2_out;

  and and_1 (and_1_out, Rd[0], Rd[1], Rd[2], Rd[3]);
  and and_2 (and_2_out, and_1_out, RegW);
  or or_1 (out_4, and_2_out, Branch);

  // Notes on the sheet:
  //   (This AND Gate returns true if input of Rd is 15), meaning  Rd == 15
  //   Rd AND RegW
  //   (Rd AND RegW) OR Branch
endmodule
