// Logisim project FidanIsmayilova_Assignment_2.circ as structural Verilog: 1 circuit, main circuit main
module main (
  input  [5:0] Func_5_0,
  input  ALUOp,
  output [1:0] FlagW_1_0,
  output [1:0] ALUControl_1_0
);

  wire and_1_out, and_2_out, and_3_out, and_4_out, and_5_out, and_6_out, and_7_out, or_1_out, or_2_out;
  wire [1:0] priority_encoder_1_out, priority_encoder_2_out;

  and and_1 (and_1_out, ~Func_5_0[1], ~Func_5_0[2], Func_5_0[3], ~Func_5_0[4]);  // AND_Gate
  and and_2 (and_2_out, ~Func_5_0[1], Func_5_0[2], ~Func_5_0[3], ~Func_5_0[4]);  // AND_Gate
  and and_3 (and_3_out, ~Func_5_0[1], ~Func_5_0[2], ~Func_5_0[3], ~Func_5_0[4]);  // AND_Gate
  and and_4 (and_4_out, ~Func_5_0[1], ~Func_5_0[2], Func_5_0[3], Func_5_0[4]);  // AND_Gate
  and and_5 (and_5_out, Func_5_0[0], or_1_out);
  or or_1 (or_1_out, and_1_out, and_2_out);
  and and_6 (and_6_out, Func_5_0[0], or_2_out);
  or or_2 (or_2_out, and_3_out, and_4_out);
  and and_7 (and_7_out, ~and_5_out, ~and_6_out);  // AND_Gate
  Priority_Encoder #(.select(2)) priority_encoder_1 (
    .in0(and_1_out), .in1(and_2_out), .in2(and_3_out), .in3(and_4_out), .out(priority_encoder_1_out));  // open: gs, en_out, en_in
  Priority_Encoder #(.select(2)) priority_encoder_2 (
    .in0(and_7_out), .in2(and_6_out), .in3(and_5_out), .out(priority_encoder_2_out));  // open: in1, gs, en_out, en_in
  Multiplexer #(.select(2), .width(2)) multiplexer_1 (
    .in0(priority_encoder_1_out), .in1(priority_encoder_1_out), .in2(priority_encoder_1_out),
    .in3(priority_encoder_1_out), .out(ALUControl_1_0), .sel(priority_encoder_1_out), .en(ALUOp));
  Multiplexer #(.select(2), .width(2)) multiplexer_2 (
    .in0(priority_encoder_2_out), .in2(priority_encoder_2_out), .in3(priority_encoder_2_out),
    .out(FlagW_1_0), .sel(priority_encoder_2_out), .en(ALUOp));  // open: in1

  // Notes on the sheet:
  //   funct0
endmodule
