// Logisim project FidanIsmayilova_Assignment_V.circ as structural Verilog: 9 circuits, main circuit Instruction Memory
module Instruction_Memory (
  input  [31:0] A,
  output [31:0] RD
);

  ROM #(.dataWidth(32)) rom_1 (.addr(A[7:0]), .data(RD));  // open: sel
endmodule

module Splitter (
  input  [31:0] RD,
  output [3:0] _31_28,
  output [1:0] _27_26,
  output [5:0] _25_20,
  output [3:0] _15_12,
  output [3:0] _19_16,
  output [3:0] _3_0,
  output [3:0] _15_12_2,
  output [23:0] _23_0
);


  assign _3_0 = RD[3:0];
  assign _15_12 = RD[15:12];
  assign _15_12_2 = RD[15:12];
  assign _19_16 = RD[19:16];
  assign _23_0 = RD[23:0];
  assign _25_20 = RD[25:20];
  assign _27_26 = RD[27:26];
  assign _31_28 = RD[31:28];
endmodule

module Data_Memory (
  input  [31:0] ALUResult,
  input  [31:0] WriteData,
  input  WE,
  output [31:0] x32
);

  wire not_1_out;

  not not_1 (not_1_out, WE);
  RAM #(.dataWidth(32), .bus("separate")) ram_1 (
    .addr(ALUResult[7:0]), .din(WriteData), .data(x32), .str(WE), .ld(not_1_out));  // open: sel, clk, clr
endmodule

module Decoder (
  input  [3:0] RD,
  input  [1:0] OP_1_0,
  input  [5:0] Func_5_0,
  output PCS,
  output MemW,
  output MemToReg,
  output ALUSrc,
  output [1:0] ImmSrc,
  output [1:0] RegSrc,
  output [1:0] FlagW_1_0,
  output [1:0] ALUControl_1_0
);

  wire main_decoder_1_aluop, main_decoder_1_branch, main_decoder_1_regw;

  Main_Decoder main_decoder_1 (
    .OP_1_0(OP_1_0), .Func_5_0(Func_5_0), .Branch(main_decoder_1_branch), .RegW(main_decoder_1_regw),
    .MemW(MemW), .MemToReg(MemToReg), .ALUScr(ALUSrc), .ImmSrc(ImmSrc), .RegSrc(RegSrc),
    .ALUOp(main_decoder_1_aluop));
  PCS pcs_1 (.Rd(RD), .RegW(main_decoder_1_regw), .Branch(main_decoder_1_branch), .PCS(PCS));
  ALU_Decoder alu_decoder_1 (
    .Func_5_0(Func_5_0), .ALUOp(main_decoder_1_aluop), .FlagW_1_0(FlagW_1_0), .ALUControl_1_0(ALUControl_1_0));
endmodule

module Extender (
  input  [23:0] _23_0,
  input  [1:0] ImmSrc,
  output [31:0] ExtImm
);

  wire [31:0] bit_extender_1_out, bit_extender_2_out, bit_extender_3_out;

  assign bit_extender_1_out = {{24{1'b0}}, _23_0[7:0]};  // Bit_Extender bit_extender_1
  assign bit_extender_2_out = {{20{1'b0}}, _23_0[11:0]};  // Bit_Extender bit_extender_2
  assign bit_extender_3_out = {{8{1'b0}}, _23_0};  // Bit_Extender bit_extender_3
  Multiplexer #(.select(2), .width(32)) multiplexer_1 (
    .in0(bit_extender_1_out), .in1(bit_extender_2_out), .in2(bit_extender_3_out), .out(ExtImm), .sel(ImmSrc));  // open: in3, en
endmodule

module Register_file (
  input  clk,
  input  [31:0] WD3,
  input  [3:0] A1,
  input  [3:0] A2,
  input  [3:0] A3,
  input  [31:0] R15,
  input  WE3,
  input  clr,
  output [31:0] RD1,
  output [31:0] RD2
);

  wire decoder_1_out0, decoder_1_out1, decoder_1_out2, decoder_1_out3, decoder_1_out4, decoder_1_out5,
       decoder_1_out6, decoder_1_out7, decoder_1_out8, decoder_1_out9, decoder_1_out10, decoder_1_out11,
       decoder_1_out12, decoder_1_out13, decoder_1_out14;
  wire [31:0] R0_q, R1_q, R2_q, R3_q, R4_q, R5_q, R6_q, R7_q, R8_q, R9_q, R10_q, R11_q, R12_q, R13_q, R14_q;

  Decoder_part #(.select(4), .disabled(0)) decoder_1 (
    .out0(decoder_1_out0), .out1(decoder_1_out1), .out2(decoder_1_out2), .out3(decoder_1_out3),
    .out4(decoder_1_out4), .out5(decoder_1_out5), .out6(decoder_1_out6), .out7(decoder_1_out7),
    .out8(decoder_1_out8), .out9(decoder_1_out9), .out10(decoder_1_out10), .out11(decoder_1_out11),
    .out12(decoder_1_out12), .out13(decoder_1_out13), .out14(decoder_1_out14), .sel(A3), .en(WE3));  // open: out15
  Register #(.width(32)) R14 (.D(WD3), .en(decoder_1_out14), .Q(R14_q), .clk(clk), .clr(clr));
  Register #(.width(32)) R13 (.D(WD3), .en(decoder_1_out13), .Q(R13_q), .clk(clk), .clr(clr));
  Register #(.width(32)) R12 (.D(WD3), .en(decoder_1_out12), .Q(R12_q), .clk(clk), .clr(clr));
  Register #(.width(32)) R11 (.D(WD3), .en(decoder_1_out11), .Q(R11_q), .clk(clk), .clr(clr));
  Register #(.width(32)) R10 (.D(WD3), .en(decoder_1_out10), .Q(R10_q), .clk(clk), .clr(clr));
  Register #(.width(32)) R9 (.D(WD3), .en(decoder_1_out9), .Q(R9_q), .clk(clk), .clr(clr));
  Register #(.width(32)) R8 (.D(WD3), .en(decoder_1_out8), .Q(R8_q), .clk(clk), .clr(clr));
  Register #(.width(32)) R7 (.D(WD3), .en(decoder_1_out7), .Q(R7_q), .clk(clk), .clr(clr));
  Register #(.width(32)) R6 (.D(WD3), .en(decoder_1_out6), .Q(R6_q), .clk(clk), .clr(clr));
  Register #(.width(32)) R5 (.D(WD3), .en(decoder_1_out5), .Q(R5_q), .clk(clk), .clr(clr));
  Register #(.width(32)) R4 (.D(WD3), .en(decoder_1_out4), .Q(R4_q), .clk(clk), .clr(clr));
  Register #(.width(32)) R2 (.D(WD3), .en(decoder_1_out2), .Q(R2_q), .clk(clk), .clr(clr));
  Register #(.width(32)) R3 (.D(WD3), .en(decoder_1_out3), .Q(R3_q), .clk(clk), .clr(clr));
  Register #(.width(32)) R1 (.D(WD3), .en(decoder_1_out1), .Q(R1_q), .clk(clk), .clr(clr));
  Register #(.width(32)) R0 (.D(WD3), .en(decoder_1_out0), .Q(R0_q), .clk(clk), .clr(clr));
  Multiplexer #(.select(4), .width(32), .enable("false")) multiplexer_1 (
    .in0(R0_q), .in1(R1_q), .in2(R2_q), .in3(R3_q), .in4(R4_q), .in5(R5_q), .in6(R6_q), .in7(R7_q),
    .in8(R8_q), .in9(R9_q), .in10(R10_q), .in11(R11_q), .in12(R12_q), .in13(R13_q), .in14(R14_q), .in15(R15),
    .out(RD1), .sel(A1));
  Multiplexer #(.select(4), .width(32), .enable("false")) multiplexer_2 (
    .in0(R0_q), .in1(R1_q), .in2(R2_q), .in3(R3_q), .in4(R4_q), .in5(R5_q), .in6(R6_q), .in7(R7_q),
    .in8(R8_q), .in9(R9_q), .in10(R10_q), .in11(R11_q), .in12(R12_q), .in13(R13_q), .in14(R14_q), .out(RD2),
    .sel(A2));  // open: in15
endmodule

module PCS (
  input  [3:0] Rd,
  input  RegW,
  input  Branch,
  output PCS
);

  wire and_1_out, and_2_out;

  and and_1 (and_1_out, Rd[0], Rd[1], Rd[2], Rd[3]);
  and and_2 (and_2_out, and_1_out, RegW);
  or or_1 (PCS, and_2_out, Branch);

  // Notes on the sheet:
  //   (This AND Gate returns true if input of Rd is 15), meaning  Rd == 15
  //   Rd AND RegW
  //   (Rd AND RegW) OR Branch
endmodule

module Main_Decoder (
  input  [1:0] OP_1_0,
  input  [5:0] Func_5_0,
  output Branch,
  output RegW,
  output MemW,
  output MemToReg,
  output ALUScr,
  output [1:0] ImmSrc,
  output [1:0] RegSrc,
  output ALUOp
);

  wire and_1_out, and_2_out, and_3_out, and_4_out, and_7_out, decoder_1_out0, decoder_1_out8, not_1_out,
       priority_encoder_1_en_out, priority_encoder_2_en_out, priority_encoder_2_out,
       priority_encoder_3_en_out, priority_encoder_3_gs;
  wire [1:0] priority_encoder_4_out;

  and and_1 (and_1_out, Func_5_0[0], and_2_out);
  Priority_Encoder #(.select(1)) priority_encoder_1 (
    .in0(OP_1_0[0]), .in1(OP_1_0[1]), .en_out(priority_encoder_1_en_out));  // open: out, gs, en_in
  Decoder_part #(.select(4)) decoder_1 (
    .out0(decoder_1_out0), .out8(decoder_1_out8), .sel(Func_5_0[4:1]));  // open: out1, out2, out3, out4, out5, out6, out7, out9, out10, out11, out12, out13, out14, out15, en
  and and_2 (and_2_out, OP_1_0[0], ~priority_encoder_1_en_out);  // AND_Gate
  and and_3 (and_3_out, priority_encoder_1_en_out, decoder_1_out8);
  and and_4 (and_4_out, decoder_1_out0, priority_encoder_1_en_out);
  and and_5 (Branch, ~OP_1_0[0], OP_1_0[1]);  // AND_Gate
  Priority_Encoder #(.select(1)) priority_encoder_2 (
    .in0(and_4_out), .in1(MemW), .out(priority_encoder_2_out), .en_out(priority_encoder_2_en_out));  // open: gs, en_in
  or or_1 (RegW, and_1_out, and_4_out, and_3_out);
  or or_2 (ALUOp, and_3_out, and_4_out);
  and and_6 (MemW, priority_encoder_3_en_out, and_2_out);
  Priority_Encoder #(.select(1)) priority_encoder_3 (
    .in1(Func_5_0[0]), .gs(priority_encoder_3_gs), .en_out(priority_encoder_3_en_out));  // open: in0, out, en_in
  or or_3 (ALUScr, Branch, and_2_out, and_3_out);
  Priority_Encoder #(.select(2)) priority_encoder_4 (
    .in0(and_3_out), .in1(and_2_out), .in2(Branch), .out(priority_encoder_4_out));  // open: in3, gs, en_out, en_in
  Multiplexer multiplexer_1 (
    .in0(priority_encoder_2_out), .in1(priority_encoder_2_out), .out(RegSrc[1]), .sel(priority_encoder_2_out));  // open: en
  and and_7 (and_7_out, priority_encoder_3_gs, and_2_out);
  Multiplexer multiplexer_2 (.in0(1'b0), .in1(and_7_out), .out(MemToReg), .sel(and_7_out), .en(not_1_out));
  not not_1 (not_1_out, MemW);
  Multiplexer #(.select(2), .width(2)) multiplexer_3 (
    .in0(priority_encoder_4_out), .in1(priority_encoder_4_out), .in2(priority_encoder_4_out),
    .in3(priority_encoder_4_out), .out(ImmSrc), .sel(priority_encoder_4_out));  // open: en

  assign RegSrc[0] = Branch;
endmodule

module ALU_Decoder (
  input  [5:0] Func_5_0,
  input  ALUOp,
  output [1:0] FlagW_1_0,
  output [1:0] ALUControl_1_0
);

  wire and_1_out, and_2_out, and_3_out, and_4_out, and_5_out, and_6_out, and_7_out, or_1_out, or_2_out;
  wire [1:0] priority_encoder_1_out, priority_encoder_2_out;

  and and_1 (and_1_out, ~Func_5_0[1], ~Func_5_0[2], Func_5_0[3], ~Func_5_0[4]);  // AND_Gate
  and and_2 (and_2_out, ~Func_5_0[1], Func_5_0[2], ~Func_5_0[3], ~Func_5_0[4]);  // AND_Gate
  and and_3 (and_3_out, ~Func_5_0[1], ~Func_5_0[2], ~Func_5_0[3], ~Func_5_0[4]);  // AND_Gate
  and and_4 (and_4_out, ~Func_5_0[1], ~Func_5_0[2], Func_5_0[3], Func_5_0[4]);  // AND_Gate
  and and_5 (and_5_out, Func_5_0[0], or_1_out);
  or or_1 (or_1_out, and_1_out, and_2_out);
  and and_6 (and_6_out, Func_5_0[0], or_2_out);
  and and_7 (and_7_out, ~and_5_out, ~and_6_out);  // AND_Gate
  or or_2 (or_2_out, and_3_out, and_4_out);
  Priority_Encoder #(.select(2)) priority_encoder_1 (
    .in0(and_1_out), .in1(and_2_out), .in2(and_3_out), .in3(and_4_out), .out(priority_encoder_1_out));  // open: gs, en_out, en_in
  Priority_Encoder #(.select(2)) priority_encoder_2 (
    .in0(and_7_out), .in2(and_6_out), .in3(and_5_out), .out(priority_encoder_2_out));  // open: in1, gs, en_out, en_in
  Multiplexer #(.select(2), .width(2)) multiplexer_1 (
    .in0(priority_encoder_1_out), .in1(priority_encoder_1_out), .in2(priority_encoder_1_out),
    .in3(priority_encoder_1_out), .out(ALUControl_1_0), .sel(priority_encoder_1_out), .en(ALUOp));
  Multiplexer #(.select(2), .width(2)) multiplexer_2 (
    .in0(priority_encoder_2_out), .in2(priority_encoder_2_out), .in3(priority_encoder_2_out),
    .out(FlagW_1_0), .sel(priority_encoder_2_out), .en(ALUOp));  // open: in1

  // Notes on the sheet:
  //   funct0
endmodule
