// Logisim project FidanIsmayilova_MainDecoder.circ as structural Verilog: 1 circuit, main circuit main
module main (
  input  [1:0] OP_1_0,
  input  [5:0] Func_5_0,
  output Branch,
  output RegW,
  output MemW,
  output MemToReg,
  output ALUScr,
  output [1:0] ImmSrc,
  output [1:0] RegSrc,
  output ALUOp
);

  wire and_1_out, and_2_out, and_3_out, and_5_out, and_7_out, decoder_1_out0, decoder_1_out1, not_1_out,
       priority_encoder_1_en_out, priority_encoder_2_en_out, priority_encoder_2_out,
       priority_encoder_3_en_out, priority_encoder_3_gs;
  wire [1:0] priority_encoder_4_out;

  and and_1 (and_1_out, Func_5_0[0], and_5_out);
  Decoder #(.select(4)) decoder_1 (
    .out0(decoder_1_out0), .out1(decoder_1_out1), .sel(Func_5_0[4:1]));  // open: out2, out3, out4, out5, out6, out7, out8, out9, out10, out11, out12, out13, out14, out15, en
  Priority_Encoder #(.select(1)) priority_encoder_1 (
    .in0(OP_1_0[0]), .in1(OP_1_0[1]), .en_out(priority_encoder_1_en_out));  // open: out, gs, en_in
  and and_2 (and_2_out, priority_encoder_1_en_out, decoder_1_out1);
  and and_3 (and_3_out, decoder_1_out0, priority_encoder_1_en_out);
  and and_4 (Branch, ~OP_1_0[0], OP_1_0[1]);  // AND_Gate
  and and_5 (and_5_out, OP_1_0[0], ~priority_encoder_1_en_out);  // AND_Gate
  or or_1 (RegW, and_1_out, and_3_out, and_2_out);
  Priority_Encoder #(.select(1)) priority_encoder_2 (
    .in0(and_3_out), .in1(MemW), .out(priority_encoder_2_out), .en_out(priority_encoder_2_en_out));  // open: gs, en_in
  or or_2 (ALUOp, and_2_out, and_3_out);
  and and_6 (MemW, priority_encoder_3_en_out, and_5_out);
  Priority_Encoder #(.select(1)) priority_encoder_3 (
    .in1(Func_5_0[0]), .gs(priority_encoder_3_gs), .en_out(priority_encoder_3_en_out));  // open: in0, out, en_in
  Multiplexer multiplexer_1 (
    .in0(priority_encoder_2_out), .in1(priority_encoder_2_out), .out(RegSrc[1]), .sel(priority_encoder_2_out));  // open: en
  and and_7 (and_7_out, priority_encoder_3_gs, and_5_out);
  or or_3 (ALUScr, Branch, and_5_out, and_2_out);
  Priority_Encoder #(.select(2)) priority_encoder_4 (
    .in0(and_2_out), .in1(and_5_out), .in2(Branch), .out(priority_encoder_4_out));  // open: in3, gs, en_out, en_in
  Multiplexer multiplexer_2 (.in0(1'b0), .in1(and_7_out), .out(MemToReg), .sel(and_7_out), .en(not_1_out));
  not not_1 (not_1_out, MemW);
  Multiplexer #(.select(2), .width(2)) multiplexer_3 (
    .in0(priority_encoder_4_out), .in1(priority_encoder_4_out), .in2(priority_encoder_4_out),
    .in3(priority_encoder_4_out), .out(ImmSrc), .sel(priority_encoder_4_out));  // open: en

  assign RegSrc[0] = Branch;
endmodule
