// Logisim project FidanIsmayilova_MainDecoder2.circ as structural Verilog: 1 circuit, main circuit main
module main (
  input  [3:0] Cond_3_0,
  input  [1:0] Flags_3_2,
  input  [1:0] Flags_1_0,
  output CondEx
);

  wire and_1_out, and_2_out, and_3_out, and_4_out, and_5_out, and_6_out, not_1_out, xor_1_out;

  and and_1 (and_1_out, ~Flags_3_2[0], not_1_out);  // AND_Gate
  and and_2 (and_2_out, ~Cond_3_0[0], ~Cond_3_0[1], ~Cond_3_0[2], ~Cond_3_0[3], Flags_3_2[0]);  // AND_Gate
  and and_3 (and_3_out, Cond_3_0[0], ~Cond_3_0[1], ~Cond_3_0[2], ~Cond_3_0[3], ~Flags_3_2[0]);  // AND_Gate
  xor xor_1 (xor_1_out, Flags_3_2[1], Flags_1_0[0]);
  not not_1 (not_1_out, xor_1_out);
  and and_4 (and_4_out, Cond_3_0[0], Cond_3_0[1], ~Cond_3_0[2], Cond_3_0[3], xor_1_out);  // AND_Gate
  and and_5 (and_5_out, ~Cond_3_0[0], Cond_3_0[1], Cond_3_0[2], Cond_3_0[3]);  // AND_Gate
  and and_6 (and_6_out, ~Cond_3_0[0], ~Cond_3_0[1], Cond_3_0[2], Cond_3_0[3], and_1_out);  // AND_Gate
  or or_1 (CondEx, and_5_out, and_2_out, and_3_out, and_4_out, and_6_out);
endmodule
